# Fritzing sketch auto_trash_bin (saved by Fritzing 0.9.3b)
breadboards: 1

parts:
  Controller = Arduino Pro Mini v13
  C1 = Electrolytic Capacitor [capacitance=2.2mF package="100 mil [THT, electrolytic]"]
  J1 = Infrared Proximity Sensor [part_number="Sharp GP2Y0A21YK0F"]
  J2 = Basic Servo [part_number=MG995]
  5V_1A = Power plug
  U1 = Voltage Regulator - 3.3V [part_number="AMS1117 3.3V" package="TO220 [THT]"]

nets:
  VCC: Controller.VCC, J1.Vcc, U1.output_voltage
  GND: Controller.GND, C1.-, J1.GND, J2.gnd, 5V_1A.GND, U1.GND
  N1: Controller.A0, J1.Vout
  N2: Controller.D9_PWM, J2.pulse
  VCC_2: C1.+, J2.vcc, 5V_1A.VCC, U1.input_voltage

notes:
  Check the pinout of your parts (regulator, servo, sensor)!
